# Fritzing sketch Esquema-de-conexiones-contador-de-monedas (saved by Fritzing 1.0.0d)
breadboards: 2

parts:
  Componente1 = Arduino Uno (Rev3)
  R1 = PHOTOCELL [package=photocell-kit]
  R2 = Resistor [tolerance=±5% power=0.25W resistance=10000 package=THT]
  J1 = Piezo Speaker
  LED1 = LED - 5mm [color="Red (660nm)" current=0.030A package="5 mm [THT]"]
  R3 = Resistor [tolerance=±5% power=0.25W resistance=10000 package=THT]
  R4 = Resistor [tolerance=±5% power=0.25W resistance=10000 package=THT]
  R5 = Resistor [tolerance=±5% power=0.25W resistance=10000 package=THT]
  R6 = Resistor [tolerance=±5% power=0.25W resistance=10000 package=THT]
  R7 = Resistor [tolerance=±5% power=0.25W resistance=10000 package=THT]
  R8 = PHOTOCELL [package=photocell-kit]
  R9 = PHOTOCELL [package=photocell-kit]
  R10 = PHOTOCELL [package=photocell-kit]
  LED2 = LED - 5mm [color="Red (660nm)" current=0.030A package="5 mm [THT]"]
  LED3 = LED - 5mm [color="Red (660nm)" current=0.030A package="5 mm [THT]"]
  LED4 = LED - 5mm [color="Red (660nm)" current=0.030A package="5 mm [THT]"]
  R11 = Resistor [tolerance=±5% power=0.25W resistance=10 package=THT]
  OLED_I2C2 = OLED 128x64 I2C Monochrome Display
  S9 = Momentary Switch 6mm 2pin
  S10 = Momentary Switch 6mm 2pin
  S11 = Momentary Switch 6mm 2pin
  S12 = Momentary Switch 6mm 2pin
  S13 = Momentary Switch 6mm 2pin
  S14 = Momentary Switch 6mm 2pin
  R12 = Resistor [tolerance=±5% power=0.25W resistance=10 package=THT]
  R13 = Resistor [tolerance=±5% power=0.25W resistance=10 package=THT]
  R14 = Resistor [tolerance=±5% power=0.25W resistance=10 package=THT]
  R15 = Resistor [tolerance=±5% power=0.25W resistance=10000 package=THT]
  R16 = Resistor [tolerance=±5% power=0.25W resistance=10000 package=THT]
  R17 = Resistor [tolerance=±5% power=0.25W resistance=10000 package=THT]
  R18 = Resistor [tolerance=±5% power=0.25W resistance=10000 package=THT]

nets:
  N1: Componente1.A0, OLED_I2C2.SCK
  N2: Componente1.A1, OLED_I2C2.SDA
  N3: Componente1.A2, R1.P$1, R15.Pin_1
  N4: Componente1.A3, R8.P$1, R16.Pin_1
  N5: Componente1.A4/SDA, R9.P$2, R17.Pin_1
  N6: Componente1.A5/SCL, R10.P$2, R18.Pin_1
  N7: Componente1.D9_PWM, J1.pin2
  GND: Componente1.GND, R2.Pin_0, J1.pin1, LED1.cathode, R3.Pin_0, R4.Pin_0, R5.Pin_0, R6.Pin_0, R7.Pin_0, LED2.cathode, LED3.cathode, LED4.cathode, OLED_I2C2.GND, R15.Pin_0, R16.Pin_0, R17.Pin_0, R18.Pin_0
  N8: Componente1.D2, R2.Pin_1, S13.1
  N9: Componente1.D3_PWM, R3.Pin_1, S14.1
  N10: Componente1.D4, R4.Pin_1, S10.1
  N11: Componente1.D5_PWM, R6.Pin_1, S12.1
  N12: Componente1.D6_PWM, R7.Pin_1, S11.1
  N13: Componente1.D7, R5.Pin_1, S9.1
  5V: Componente1.5V, R1.P$2, R8.P$2, R9.P$1, R10.P$1, R11.Pin_1, OLED_I2C2.VDD, S9.2, S10.2, S11.2, S12.2, S13.2, S14.2, R12.Pin_1, R13.Pin_1, R14.Pin_1
  N14: LED1.anode, R14.Pin_0
  N15: LED2.anode, R11.Pin_0
  N16: LED3.anode, R13.Pin_0
  N17: LED4.anode, R12.Pin_0

custom parts:
  Momentary Switch 6mm 2pin: Momentary Switch 6mm 2 pin Button commonly used for reset or general input.
